// Digital circuit 1-bit-full-adder.dig as structural Verilog
module _1_bit_full_adder (
  input  a,
  input  b,
  input  cin,
  output cout,
  output sum
);

  wire and_1_out, and_2_out, xor_1_out;

  xor xor_1 (xor_1_out, a, b);
  and and_1 (and_1_out, a, b);
  xor xor_2 (sum, xor_1_out, cin);
  and and_2 (and_2_out, xor_1_out, cin);
  or or_1 (cout, and_2_out, and_1_out);
endmodule
