// Digital circuit 8-bit-ripple-carry-adder.dig as structural Verilog
module _8_bit_ripple_carry_adder (
  input  cin,
  input  [7:0] a,
  input  [7:0] b,
  output [7:0] sum,
  output cout
);

  wire _1_bit_full_adder_1_cout, _1_bit_full_adder_2_cout, _1_bit_full_adder_3_cout,
       _1_bit_full_adder_4_cout, _1_bit_full_adder_5_cout, _1_bit_full_adder_6_cout, _1_bit_full_adder_7_cout;

  _1_bit_full_adder _1_bit_full_adder_1 (.a(a[0]), .b(b[0]), .cin(cin), .cout(_1_bit_full_adder_1_cout), .sum(sum[0]));
  _1_bit_full_adder _1_bit_full_adder_2 (
    .a(a[1]), .b(b[1]), .cin(_1_bit_full_adder_1_cout), .cout(_1_bit_full_adder_2_cout), .sum(sum[1]));
  _1_bit_full_adder _1_bit_full_adder_3 (
    .a(a[2]), .b(b[2]), .cin(_1_bit_full_adder_2_cout), .cout(_1_bit_full_adder_3_cout), .sum(sum[2]));
  _1_bit_full_adder _1_bit_full_adder_4 (
    .a(a[3]), .b(b[3]), .cin(_1_bit_full_adder_3_cout), .cout(_1_bit_full_adder_4_cout), .sum(sum[3]));
  _1_bit_full_adder _1_bit_full_adder_5 (
    .a(a[4]), .b(b[4]), .cin(_1_bit_full_adder_4_cout), .cout(_1_bit_full_adder_5_cout), .sum(sum[4]));
  _1_bit_full_adder _1_bit_full_adder_6 (
    .a(a[5]), .b(b[5]), .cin(_1_bit_full_adder_5_cout), .cout(_1_bit_full_adder_6_cout), .sum(sum[5]));
  _1_bit_full_adder _1_bit_full_adder_7 (
    .a(a[6]), .b(b[6]), .cin(_1_bit_full_adder_6_cout), .cout(_1_bit_full_adder_7_cout), .sum(sum[6]));
  _1_bit_full_adder _1_bit_full_adder_8 (.a(a[7]), .b(b[7]), .cin(_1_bit_full_adder_7_cout), .cout(cout), .sum(sum[7]));
endmodule
