// Digital circuit instruction_memory.dig as structural Verilog
module instruction_memory (
  input  [7:0] A,
  input  [1:0] PROG,
  output [31:0] D
);

  wire [31:0] add_imm_d, cumulative_d, mov_imm_d, sub_imm_d;

  ROM #(.AddrBits(8), .Bits(32)) add_imm (.A(A), .sel(1'b1), .D(add_imm_d));
  ROM #(.AddrBits(8), .Bits(32)) cumulative (.A(A), .sel(1'b1), .D(cumulative_d));
  ROM #(.AddrBits(8), .Bits(32)) mov_imm (.A(A), .sel(1'b1), .D(mov_imm_d));
  ROM #(.AddrBits(8), .Bits(32)) sub_imm (.A(A), .sel(1'b1), .D(sub_imm_d));
  Multiplexer #(.Selector_Bits(2), .Bits(32)) multiplexer_1 (
    .sel(PROG), .in_0(add_imm_d), .in_1(cumulative_d), .in_2(mov_imm_d), .in_3(sub_imm_d), .out(D));
endmodule
