// Digital circuit lab05.dig as structural Verilog
module lab05 (
  input  CLK,
  input  [1:0] PROG,
  input  CLR,
  input  [4:0] RR0,
  input  [4:0] RR1,
  input  WE,
  input  [4:0] WR,
  input  [63:0] Imm,
  input  ALUSrcB,
  input  [3:0] ALUOp,
  output [63:0] T0,
  output [63:0] T1
);

  wire [31:0] iw;
  wire [63:0] _64bit_register_1_q, add_1_s, alu_1_r, multiplexer_1_out, register_file_1_rd0,
       register_file_1_rd1, x0, x1, x2, x3, x4, x7, x8, x9, x10, x11, x12, x13, x14, x15, x16, x17, x18, x19,
       x20, x21, x22, x23, x24, x25, x26, x27, x28, x29, x30, x31;

  _64bit_register _64bit_register_1 (.Q(_64bit_register_1_q), .D(add_1_s), .CLK(CLK), .EN(1'b1), .CLR(CLR));
  instruction_memory instruction_memory_1 (.A(_64bit_register_1_q[7:0]), .D(iw), .PROG(PROG));
  Add #(.Bits(64)) add_1 (.a(_64bit_register_1_q), .b(64'h4), .c_i(1'b0), .s(add_1_s));  // open: c_o
  register_file register_file_1 (
    .ReadReg0(RR0), .ReadReg1(RR1), .WriteEn(WE), .WriteReg(WR), .WriteData(alu_1_r), .CLK(CLK), .CLR(CLR),
    .RD0(register_file_1_rd0), .RD1(register_file_1_rd1), .x0(x0), .x1(x1), .x2(x2), .x3(x3), .x4(x4),
    .x5(T0), .x6(T1), .x7(x7), .x8(x8), .x9(x9), .x10(x10), .x11(x11), .x12(x12), .x13(x13), .x14(x14),
    .x15(x15), .x16(x16), .x17(x17), .x18(x18), .x19(x19), .x20(x20), .x21(x21), .x22(x22), .x23(x23),
    .x24(x24), .x25(x25), .x26(x26), .x27(x27), .x28(x28), .x29(x29), .x30(x30), .x31(x31));
  Multiplexer #(.Bits(64)) multiplexer_1 (
    .sel(ALUSrcB), .in_0(register_file_1_rd1), .in_1(Imm), .out(multiplexer_1_out));
  alu alu_1 (.A(register_file_1_rd0), .B(multiplexer_1_out), .ALUOp(ALUOp), .R(alu_1_r));

  // Other names for the same wires on the sheet: x5[63:0] = T0; x6[63:0] = T1
endmodule

/* Test case add-imm:
CLK CLR RR0 RR1 WR WE ALUOp ALUSrcB Imm T0
0   1   0   0   0  1  0     1       1   x
0   0   0   0   5  1  0     1       1   x
1   0   0   0   5  1  0     1       1   1
*/

/* Test case move-imm:
CLK CLR RR0 RR1 WR WE ALUOp ALUSrcB Imm T1
0   1   0   0   6  1  0     1       2   x
0   0   0   0   6  1  0     1       2   x
1   0   0   0   6  1  0     1       2   2
*/

/* Test case cumulative:
CLK CLR RR0 RR1 WR WE ALUOp ALUSrcB Imm T0 T1
0   1   0   5   5  1  0     1       1   x  x
0   0   0   5   5  1  0     1       1   x  x
1   0   0   5   5  1  0     1       1   1  x
0   0   0   5   6  1  0     1       1   x  x
1   0   0   5   6  1  0     1       1   x  1
0   0   5   6   5  1  1     0       0   x  x
1   0   5   6   5  1  1     0       0   0  x
*/

/* Test case sub-imm:
CLK CLR RR0 RR1 WR WE ALUOp ALUSrcB Imm T0
0   1   0   0   0  1  1     1       1   x
0   0   0   0   5  1  1     1       1   x
1   0   0   0   5  1  1     1       1   0xFFFFFFFFFFFFFFFF
*/
