// Digital circuit InstDecoder.dig as structural Verilog
module InstDecoder (
  input  [31:0] IW,
  output WDsel,
  output PCsel,
  output [1:0] ALUSrcB,
  output ALUSrcA,
  output [2:0] ALUOp,
  output RFW
);

  wire add_2_eq, add_3_eq, add_eq, and_1_out, and_2_out, and_3_out, i_type_eq, i_type_jalr_eq, j_type_eq,
       jalr_eq, r_type_eq;
  wire [1:0] priorityencoder_1_num;

  Comparator #(.Bits(7)) i_type (.a(IW[6:0]), .b(7'b0010011), .eq(i_type_eq));  // open: gt, lt
  Comparator #(.Bits(7)) r_type (.a(IW[6:0]), .b(7'b0110011), .eq(r_type_eq));  // open: gt, lt
  Comparator #(.Bits(7)) j_type (.a(IW[6:0]), .b(7'b1101111), .eq(j_type_eq));  // open: gt, lt
  Comparator #(.Bits(7)) i_type_jalr (.a(IW[6:0]), .b(7'b1100111), .eq(i_type_jalr_eq));  // open: gt, lt
  Comparator #(.Bits(3)) add (.a(IW[14:12]), .b(3'b000), .eq(add_eq));  // open: gt, lt
  Comparator #(.Bits(3)) add_2 (.a(IW[14:12]), .b(3'b000), .eq(add_2_eq));  // open: gt, lt
  Comparator #(.Bits(7)) add_3 (.a(IW[31:25]), .b({7{1'b0}}), .eq(add_3_eq));  // open: gt, lt
  Comparator #(.Bits(3)) jalr (.a(IW[14:12]), .b(3'b000), .eq(jalr_eq));  // open: gt, lt
  and and_1 (and_1_out, i_type_eq, add_eq);
  and and_2 (and_2_out, r_type_eq, add_2_eq, add_3_eq);
  and and_3 (and_3_out, i_type_jalr_eq, jalr_eq);
  PriorityEncoder #(.Selector_Bits(2)) priorityencoder_1 (
    .in0(and_1_out), .in1(and_2_out), .in2(j_type_eq), .in3(and_3_out), .num(priorityencoder_1_num));  // open: any
  ROM #(.Bits(9)) rom_1 (.A(priorityencoder_1_num), .sel(1'b1), .D({RFW, ALUOp, ALUSrcA, ALUSrcB, PCsel, WDsel}));

  // Other names for the same wires on the sheet: opcode[6:0] = IW[6:0]; funct3[2:0] = IW[14:12];
  //   funct7[6:0] = IW[31:25]

  // Notes on the sheet:
  //   contents of rom_1 (hex, n*v repeats v):
  //   104,100,11b,107
endmodule
