// Digital circuit 1bit-reg-clr-en.dig as structural Verilog
module _1bit_reg_clr_en (
  input  D,
  input  CLK,
  input  CLR,
  input  EN,
  output Q,
  output nQ
);

  wire dlatch_clr_1_q, multiplexer_1_out, not_1_out;

  Multiplexer multiplexer_1 (.sel(EN), .in_0(Q), .in_1(D), .out(multiplexer_1_out));
  not not_1 (not_1_out, CLK);
  dlatch_clr dlatch_clr_1 (.D(multiplexer_1_out), .CLK(not_1_out), .CLR(CLR), .Q(dlatch_clr_1_q));  // open: nQ
  dlatch_clr dlatch_clr_2 (.D(dlatch_clr_1_q), .CLK(CLK), .CLR(CLR), .Q(Q), .nQ(nQ));
endmodule
