// Digital circuit 5bit-comparator.dig as structural Verilog
module _5bit_comparator (
  input  [4:0] A,
  input  [4:0] B,
  output EQ
);

  wire _1bit_comparator_1_eq, _1bit_comparator_2_eq, _1bit_comparator_3_eq, _1bit_comparator_4_eq,
       _1bit_comparator_5_eq;

  _1bit_comparator _1bit_comparator_1 (.A(A[0]), .B(B[0]), .EQ(_1bit_comparator_1_eq));
  _1bit_comparator _1bit_comparator_2 (.A(A[1]), .B(B[1]), .EQ(_1bit_comparator_2_eq));
  _1bit_comparator _1bit_comparator_3 (.A(A[2]), .B(B[2]), .EQ(_1bit_comparator_3_eq));
  _1bit_comparator _1bit_comparator_4 (.A(A[3]), .B(B[3]), .EQ(_1bit_comparator_4_eq));
  _1bit_comparator _1bit_comparator_5 (.A(A[4]), .B(B[4]), .EQ(_1bit_comparator_5_eq));
  and and_1 (EQ, _1bit_comparator_1_eq, _1bit_comparator_2_eq, _1bit_comparator_3_eq, _1bit_comparator_4_eq, _1bit_comparator_5_eq);
endmodule
