// Digital circuit 8bit_register_clr_en.dig as structural Verilog
module _8bit_register_clr_en (
  input  [7:0] D,
  input  CLK,
  input  CLR,
  input  EN,
  output [7:0] Q
);

  _1bit_reg_clr_en _1bit_reg_clr_en_1 (.D(D[0]), .CLK(CLK), .EN(EN), .CLR(CLR), .Q(Q[0]));  // open: nQ
  _1bit_reg_clr_en _1bit_reg_clr_en_2 (.D(D[1]), .CLK(CLK), .EN(EN), .CLR(CLR), .Q(Q[1]));  // open: nQ
  _1bit_reg_clr_en _1bit_reg_clr_en_3 (.D(D[2]), .CLK(CLK), .EN(EN), .CLR(CLR), .Q(Q[2]));  // open: nQ
  _1bit_reg_clr_en _1bit_reg_clr_en_4 (.D(D[3]), .CLK(CLK), .EN(EN), .CLR(CLR), .Q(Q[3]));  // open: nQ
  _1bit_reg_clr_en _1bit_reg_clr_en_5 (.D(D[4]), .CLK(CLK), .EN(EN), .CLR(CLR), .Q(Q[4]));  // open: nQ
  _1bit_reg_clr_en _1bit_reg_clr_en_6 (.D(D[5]), .CLK(CLK), .EN(EN), .CLR(CLR), .Q(Q[5]));  // open: nQ
  _1bit_reg_clr_en _1bit_reg_clr_en_7 (.D(D[6]), .CLK(CLK), .EN(EN), .CLR(CLR), .Q(Q[6]));  // open: nQ
  _1bit_reg_clr_en _1bit_reg_clr_en_8 (.D(D[7]), .CLK(CLK), .EN(EN), .CLR(CLR), .Q(Q[7]));  // open: nQ
endmodule
