// Digital circuit analyze_decode.dig as structural Verilog
module analyze_decode (
  input  [31:0] IW,
  output [2:0] inum
);

  wire _5bit_comparator_1_eq, _7bit_comparator_1_eq, _7bit_comparator_2_eq, _7bit_comparator_3_eq,
       _7bit_comparator_4_eq, _7bit_comparator_5_eq, _7bit_comparator_6_eq, _7bit_comparator_7_eq, and_1_out;

  _7bit_comparator _7bit_comparator_1 (.A(IW[6:0]), .B(7'b0010011), .EQ(_7bit_comparator_1_eq));
  _7bit_comparator _7bit_comparator_2 (.A(IW[6:0]), .B(7'b0110011), .EQ(_7bit_comparator_2_eq));
  _7bit_comparator _7bit_comparator_3 (.A(IW[6:0]), .B(7'b0000011), .EQ(_7bit_comparator_3_eq));
  _7bit_comparator _7bit_comparator_4 (.A(IW[6:0]), .B(7'b0100011), .EQ(_7bit_comparator_4_eq));
  _7bit_comparator _7bit_comparator_5 (.A(IW[6:0]), .B(7'b1100011), .EQ(_7bit_comparator_5_eq));
  _7bit_comparator _7bit_comparator_6 (.A(IW[6:0]), .B(7'b1100111), .EQ(_7bit_comparator_6_eq));
  _7bit_comparator _7bit_comparator_7 (.A(IW[6:0]), .B(7'b1101111), .EQ(_7bit_comparator_7_eq));
  _5bit_comparator _5bit_comparator_1 (.A(IW[11:7]), .B({5{1'b0}}), .EQ(_5bit_comparator_1_eq));
  and and_1 (and_1_out, _7bit_comparator_7_eq, _5bit_comparator_1_eq);
  PriorityEncoder #(.Selector_Bits(3)) priorityencoder_1 (
    .in0(_7bit_comparator_1_eq), .in1(_7bit_comparator_2_eq), .in2(_7bit_comparator_3_eq),
    .in3(_7bit_comparator_4_eq), .in4(_7bit_comparator_5_eq), .in5(_7bit_comparator_7_eq), .in6(and_1_out),
    .in7(_7bit_comparator_6_eq), .num(inum));  // open: any
endmodule
