// Digital circuit dflipflop.dig as structural Verilog
module dflipflop (
  input  D,
  input  CLK,
  output Q,
  output nQ
);

  wire dlatch_1_q, not_1_out;

  not not_1 (not_1_out, CLK);
  dlatch dlatch_1 (.D(D), .CLK(not_1_out), .Q(dlatch_1_q));  // open: nQ
  dlatch dlatch_2 (.D(dlatch_1_q), .CLK(CLK), .Q(Q), .nQ(nQ));
endmodule
