// Digital circuit project05.dig as structural Verilog
module project05 (
  input  [1:0] PROG,
  input  CLR,
  input  CLK,
  output [7:0] ITYPE,
  output [7:0] RTYPE,
  output [7:0] LOAD,
  output [7:0] STYPE,
  output [7:0] BTYPE,
  output [7:0] JAL,
  output [7:0] J,
  output [7:0] JALR,
  output [7:0] TOTAL,
  output DONE
);

  wire and_1_out, decoder_1_out_0, decoder_1_out_1, decoder_1_out_2, decoder_1_out_3, decoder_1_out_4,
       decoder_1_out_5, decoder_1_out_6, decoder_1_out_7;
  wire [2:0] analyze_decode_1_inum;
  wire [7:0] _8bit_adder_1_sum, multiplexer_1_out;
  wire [31:0] instruction_memory_1_d;

  and and_1 (and_1_out, CLK, ~DONE);  // And
  _8bit_counter _8bit_counter_1 (.CLK(and_1_out), .CLR(CLR), .COUNT(TOTAL));
  instruction_memory instruction_memory_1 (.A(TOTAL), .D(instruction_memory_1_d), .PIN(PROG));
  _32bit_eq _32bit_eq_1 (.A(instruction_memory_1_d), .B(32'hc0001073), .EQ(DONE));
  analyze_decode analyze_decode_1 (.IW(instruction_memory_1_d), .inum(analyze_decode_1_inum));
  Decoder #(.Selector_Bits(3)) decoder_1 (
    .sel(analyze_decode_1_inum), .out_0(decoder_1_out_0), .out_1(decoder_1_out_1), .out_2(decoder_1_out_2),
    .out_3(decoder_1_out_3), .out_4(decoder_1_out_4), .out_5(decoder_1_out_5), .out_6(decoder_1_out_6),
    .out_7(decoder_1_out_7));
  _8bit_adder _8bit_adder_1 (.A(8'h1), .B(multiplexer_1_out), .Sum(_8bit_adder_1_sum));
  _8bit_register_clr_en _8bit_register_clr_en_1 (
    .D(_8bit_adder_1_sum), .CLK(and_1_out), .EN(decoder_1_out_0), .CLR(CLR), .Q(ITYPE));
  _8bit_register_clr_en _8bit_register_clr_en_2 (
    .D(_8bit_adder_1_sum), .CLK(and_1_out), .EN(decoder_1_out_1), .CLR(CLR), .Q(RTYPE));
  _8bit_register_clr_en _8bit_register_clr_en_3 (
    .D(_8bit_adder_1_sum), .CLK(and_1_out), .EN(decoder_1_out_2), .CLR(CLR), .Q(LOAD));
  _8bit_register_clr_en _8bit_register_clr_en_4 (
    .D(_8bit_adder_1_sum), .CLK(and_1_out), .EN(decoder_1_out_3), .CLR(CLR), .Q(STYPE));
  _8bit_register_clr_en _8bit_register_clr_en_5 (
    .D(_8bit_adder_1_sum), .CLK(and_1_out), .EN(decoder_1_out_4), .CLR(CLR), .Q(BTYPE));
  _8bit_register_clr_en _8bit_register_clr_en_6 (
    .D(_8bit_adder_1_sum), .CLK(and_1_out), .EN(decoder_1_out_5), .CLR(CLR), .Q(JAL));
  _8bit_register_clr_en _8bit_register_clr_en_7 (
    .D(_8bit_adder_1_sum), .CLK(and_1_out), .EN(decoder_1_out_6), .CLR(CLR), .Q(J));
  _8bit_register_clr_en _8bit_register_clr_en_8 (
    .D(_8bit_adder_1_sum), .CLK(and_1_out), .EN(decoder_1_out_7), .CLR(CLR), .Q(JALR));
  Multiplexer #(.Selector_Bits(3), .Bits(8)) multiplexer_1 (
    .sel(analyze_decode_1_inum), .in_0(ITYPE), .in_1(RTYPE), .in_2(LOAD), .in_3(STYPE), .in_4(BTYPE),
    .in_5(JAL), .in_6(J), .in_7(JALR), .out(multiplexer_1_out));
endmodule
