// Digital circuit ALU.dig as structural Verilog
module ALU (
  input  [63:0] A,
  input  [63:0] B,
  input  [3:0] ALUOp,
  output [63:0] R
);

  wire [31:0] ADDW_s;
  wire [63:0] add_1_s, and_1_out, barrelshifter_1_out, bitextender_1_out, mul_1_mul, or_1_out, SR_out,
       sub_1_s;

  Add #(.Bits(64)) add_1 (.a(A), .b(B), .c_i(1'b0), .s(add_1_s));  // open: c_o
  Sub #(.Bits(64)) sub_1 (.a(A), .b(B), .c_i(1'b0), .s(sub_1_s));  // open: c_o
  Mul #(.Bits(32)) mul_1 (.a(A[31:0]), .b(B[31:0]), .mul(mul_1_mul));
  BarrelShifter #(.Bits(64)) barrelshifter_1 (.in(A), .shift(B[6:0]), .out(barrelshifter_1_out));
  BarrelShifter #(.Bits(64), .direction("right")) SR (.in(A), .shift(B[6:0]), .out(SR_out));
  assign and_1_out = A & B;  // And and_1, 64 bits wide
  assign or_1_out = A | B;  // Or or_1, 64 bits wide
  Add #(.Bits(32)) ADDW (.a(A[31:0]), .b(B[31:0]), .c_i(1'b0), .s(ADDW_s));  // open: c_o
  BitExtender #(.inputBits(32), .outputBits(64)) bitextender_1 (.in(ADDW_s), .out(bitextender_1_out));
  Multiplexer #(.Selector_Bits(4), .Bits(64)) multiplexer_1 (
    .sel(ALUOp), .in_0(add_1_s), .in_1(sub_1_s), .in_2(mul_1_mul), .in_3(barrelshifter_1_out), .in_4(SR_out),
    .in_5(and_1_out), .in_6(or_1_out), .in_7(bitextender_1_out), .in_8(B), .in_9({64{1'b0}}),
    .in_10({64{1'b0}}), .in_11({64{1'b0}}), .in_12({64{1'b0}}), .in_13({64{1'b0}}), .in_14({64{1'b0}}),
    .in_15({64{1'b0}}), .out(R));
endmodule
