// Digital circuit Branch_Unit.dig as structural Verilog
module Branch_Unit (
  input  [63:0] A,
  input  [63:0] B,
  input  [2:0] BROp,
  input  PCSel,
  output PCBr
);

  wire BEQ_eq, BGE_eq, BGE_gt, BLT_lt, BNE_eq, multiplexer_1_out, not_1_out, or_1_out;

  Comparator #(.Bits(64)) BEQ (.a(A), .b(B), .eq(BEQ_eq));  // open: gt, lt
  Comparator #(.Bits(64)) BNE (.a(A), .b(B), .eq(BNE_eq));  // open: gt, lt
  Comparator #(.Bits(64)) BGE (.a(A), .b(B), .gt(BGE_gt), .eq(BGE_eq));  // open: lt
  Comparator #(.Bits(64)) BLT (.a(A), .b(B), .lt(BLT_lt));  // open: gt, eq
  not not_1 (not_1_out, BNE_eq);
  or or_1 (or_1_out, BGE_gt, BGE_eq);
  Multiplexer #(.Selector_Bits(3)) multiplexer_1 (
    .sel(BROp), .in_0(1'b0), .in_1(BEQ_eq), .in_2(not_1_out), .in_3(or_1_out), .in_4(BLT_lt), .in_5(1'b0),
    .in_6(1'b0), .in_7(1'b0), .out(multiplexer_1_out));
  or or_2 (PCBr, multiplexer_1_out, PCSel);
endmodule
