// Digital circuit inst-mem.dig as structural Verilog
module inst_mem (
  input  [7:0] ADDR,
  input  [4:0] PROG,
  output [31:0] IW
);

  wire [31:0] _00, _01, _02, _03, _04, _05, _06, _07, _08, _09, _10, _11, _12, _13, _14, _15, _16, _17, _18,
       _19, _20, _21, _22, _23;

  ROM #(.AddrBits(8), .Bits(32)) unit_add_i (.A(ADDR), .sel(1'b1), .D(_00));
  ROM #(.AddrBits(8), .Bits(32)) unit_add_r (.A(ADDR), .sel(1'b1), .D(_01));
  ROM #(.AddrBits(8), .Bits(32)) unit_jal (.A(ADDR), .sel(1'b1), .D(_02));
  ROM #(.AddrBits(8), .Bits(32)) unit_mul (.A(ADDR), .sel(1'b1), .D(_03));
  ROM #(.AddrBits(8), .Bits(32)) unit_sll_r (.A(ADDR), .sel(1'b1), .D(_04));
  ROM #(.AddrBits(8), .Bits(32)) unit_srl_r (.A(ADDR), .sel(1'b1), .D(_05));
  ROM #(.AddrBits(8), .Bits(32)) unit_slli (.A(ADDR), .sel(1'b1), .D(_06));
  ROM #(.AddrBits(8), .Bits(32)) unit_srli (.A(ADDR), .sel(1'b1), .D(_07));
  ROM #(.AddrBits(8), .Bits(32)) unit_j (.A(ADDR), .sel(1'b1), .D(_08));
  ROM #(.AddrBits(8), .Bits(32)) unit_beq (.A(ADDR), .sel(1'b1), .D(_09));
  ROM #(.AddrBits(8), .Bits(32)) unit_blt (.A(ADDR), .sel(1'b1), .D(_10));
  ROM #(.AddrBits(8), .Bits(32)) unit_bge (.A(ADDR), .sel(1'b1), .D(_11));
  ROM #(.AddrBits(8), .Bits(32)) unit_sd_ld (.A(ADDR), .sel(1'b1), .D(_12));
  ROM #(.AddrBits(8), .Bits(32)) unit_sw_lw (.A(ADDR), .sel(1'b1), .D(_13));
  ROM #(.AddrBits(8), .Bits(32)) unit_sb_lb (.A(ADDR), .sel(1'b1), .D(_14));
  ROM #(.AddrBits(8), .Bits(32)) unit_prog_quadratic (.A(ADDR), .sel(1'b1), .D(_15));
  ROM #(.AddrBits(8), .Bits(32)) unit_prog_get_bitseq (.A(ADDR), .sel(1'b1), .D(_16));
  ROM #(.AddrBits(8), .Bits(32)) unit_prog_fibrec (.A(ADDR), .sel(1'b1), .D(_17));
  ROM #(.AddrBits(8), .Bits(32)) unit_prog_ispal (.A(ADDR), .sel(1'b1), .D(_18));
  ROM #(.AddrBits(8), .Bits(32)) unit_prog_to_upper (.A(ADDR), .sel(1'b1), .D(_19));
  ROM #(.AddrBits(8), .Bits(32)) unit_prog_swap (.A(ADDR), .sel(1'b1), .D(_20));
  ROM #(.AddrBits(8), .Bits(32)) unit_prog_sort (.A(ADDR), .sel(1'b1), .D(_21));
  ROM #(.AddrBits(8), .Bits(32)) unit_prog_rstr (.A(ADDR), .sel(1'b1), .D(_22));
  ROM #(.AddrBits(8), .Bits(32)) unit_prog_countll (.A(ADDR), .sel(1'b1), .D(_23));
  Multiplexer #(.Selector_Bits(5), .Bits(32)) multiplexer_1 (
    .sel(PROG), .in_0(_00), .in_1(_01), .in_2(_02), .in_3(_03), .in_4(_04), .in_5(_05), .in_6(_06),
    .in_7(_07), .in_8(_08), .in_9(_09), .in_10(_10), .in_11(_11), .in_12(_12), .in_13(_13), .in_14(_14),
    .in_15(_15), .in_16(_16), .in_17(_17), .in_18(_18), .in_19(_19), .in_20(_20), .in_21(_21), .in_22(_22),
    .in_23(_23), .in_24({32{1'b0}}), .in_25({32{1'b0}}), .in_26({32{1'b0}}), .in_27({32{1'b0}}),
    .in_28({32{1'b0}}), .in_29({32{1'b0}}), .in_30({32{1'b0}}), .in_31({32{1'b0}}), .out(IW));

  // Notes on the sheet:
  //   contents of unit_add_i (hex, n*v repeats v):
  //   100513,250513,c0001073
  //   contents of unit_add_r (hex, n*v repeats v):
  //   300513,600593,b50533,c0001073
  //   contents of unit_jal (hex, n*v repeats v):
  //   100513,200593,8000ef,c0001073,b50533,8067
  //   contents of unit_mul (hex, n*v repeats v):
  //   300513,700593,2b50533,c0001073
  //   contents of unit_sll_r (hex, n*v repeats v):
  //   100593,200613,c59533,c0001073
  //   contents of unit_srl_r (hex, n*v repeats v):
  //   800593,100613,c5d533,c0001073
  //   contents of unit_slli (hex, n*v repeats v):
  //   100593,359513,c0001073
  //   contents of unit_srli (hex, n*v repeats v):
  //   2000593,25d513,c0001073
  //   contents of unit_j (hex, n*v repeats v):
  //   100513,80006f,513,c0001073
  //   contents of unit_beq (hex, n*v repeats v):
  //   100513,100593,b50463,513,c0001073
  //   contents of unit_blt (hex, n*v repeats v):
  //   100513,200593,b54463,513,c0001073
  //   contents of unit_bge (hex, n*v repeats v):
  //   200513,100593,b55463,513,c0001073
  //   contents of unit_sd_ld (hex, n*v repeats v):
  //   8000113,ff810113,513,6300293,513023,13503,c0001073
  //   contents of unit_sw_lw (hex, n*v repeats v):
  //   8000113,ff810113,513,6300293,512023,12503,c0001073
  //   contents of unit_sb_lb (hex, n*v repeats v):
  //   8000113,ff810113,513,6300293,5101a3,310503,c0001073
  //   contents of unit_prog_quadratic (hex, n*v repeats v):
  //   200513,300593,400613,500693,8000ef,c0001073,2a502b3,2b282b3,2c50333
  //   ,628533,d50533,8067
  //   contents of unit_prog_get_bitseq (hex, n*v repeats v):
  //   513,1650513,851513,fa50513,451513,550513,c00593,f00613,8000ef
  //   ,c0001073,40b602b3,128293,4000393,729863,50313,fff00393,140006f
  //   ,b55333,100393,5393b3,fff38393,737533,8067
  //   contents of unit_prog_fibrec (hex, n*v repeats v):
  //   40000113,a00513,8000ef,c0001073,100293,a2c463,8067,fe810113,113023
  //   ,a13423,fff50513,fe5ff0ef,a13823,813503,ffe50513,fd5ff0ef,1013303
  //   ,650533,13083,1810113,8067
  //   contents of unit_prog_ispal (hex, n*v repeats v):
  //   40000113,ff810113,7200293,510023,6100293,5100a3,6300293,510123
  //   ,6500293,5101a3,6300293,510223,6100293,5102a3,7200293,510323,103a3
  //   ,200533,593,600613,8000ef,c0001073,c5c663,100513,3c0006f,b502b3
  //   ,28283,c50333,30303,628663,513,200006f,ff810113,113023,158593
  //   ,fff60613,fc9ff0ef,13083,810113,8067
  //   contents of unit_prog_to_upper (hex, n*v repeats v):
  //   40000113,ff810113,4600293,510023,6f00293,5100a3,6f00293,510123
  //   ,4200293,5101a3,6100293,510223,7200293,5102a3,10323,200533,ff810113
  //   ,2005b3,2004b3,3c000ef,913,293,800313,3800393,2628063,48e03,7e1e33
  //   ,1c96933,148493,128293,ff838393,fe5ff06f,1200533,c0001073,6100313
  //   ,7b00393,50283,2028063,62c663,72d463,fe028293,558023,150513,158593
  //   ,fe1ff06f,58023,8067
  //   contents of unit_prog_swap (hex, n*v repeats v):
  //   40000113,fe010113,200293,512023,800293,512223,600293,512423,400293
  //   ,512623,a00293,512823,c00293,512a23,200533,2004b3,100593,500613
  //   ,18000ef,412503,c0001073,13,13,13,400293,2558333,650333,25603b3
  //   ,7503b3,32e03,3ae83,1d32023,1c3a023,8067
  //   contents of unit_prog_sort (hex, n*v repeats v):
  //   40000113,fe010113,200293,512023,800293,512223,600293,512423,400293
  //   ,512623,a00293,512823,c00293,512a23,200533,2004b3,400593,38000ef
  //   ,4a503,2051513,44a283,556533,84a583,2059593,c4a283,55e5b3,104a603
  //   ,2061613,144a283,566633,c0001073,fd810113,113023,100293,6b2d263
  //   ,28313,4605a63,400e13,3c30eb3,1d50f33,ffcf0f93,f2f03,faf83,3ff5c63
  //   ,a13423,b13823,513c23,2613023,30593,fff30613,30000ef,813503,1013583
  //   ,1813283,2013303,fff30313,fb1ff06f,128293,fa1ff06f,13083,2810113
  //   ,8067,400293,2558333,650333,25603b3,7503b3,32e03,3ae83,1d32023
  //   ,1c3a023,8067
  //   contents of unit_prog_rstr (hex, n*v repeats v):
  //   40000113,ff810113,4600293,510023,6f00293,5100a3,6f00293,510123
  //   ,4200293,5101a3,6100293,510223,7200293,5102a3,10323,103a3,2005b3
  //   ,ff810113,200533,2004b3,5c000ef,913,293,800313,3800393,2628063
  //   ,48e03,7e1e33,1c96933,148493,128293,ff838393,fe5ff06f,1200533
  //   ,c0001073,293,50303,30863,128293,150513,ff1ff06f,28513,8067,fe010113
  //   ,113023,a13423,b13823,58513,fcdff0ef,50293,813503,1013583,313
  //   ,28393,fff38393,2535063,758eb3,e8f03,650eb3,1ee8023,130313,fff38393
  //   ,fe5ff06f,f13,550eb3,1ee8023,13083,2010113,8067
  //   contents of unit_prog_countll (hex, n*v repeats v):
  //   40000113,fd010113,b00293,512423,1010293,513023,1600293,512c23
  //   ,2010293,513823,1600293,2512423,293,2513023,200533,8000ef,c0001073
  //   ,293,50863,128293,53503,ff5ff06f,28513,8067
endmodule
