// Digital circuit inum.dig as structural Verilog
module inum (
  input  [4:0] inum,
  output [7:0] c0,
  output [7:0] c1,
  output [7:0] c2,
  output [7:0] c3
);

  ROM #(.AddrBits(5), .Bits(32)) rom_1 (.A(inum), .sel(1'b1), .D({c0, c1, c2, c3}));

  // Notes on the sheet:
  //   contents of rom_1 (hex, n*v repeats v):
  //   41444449,41444452,4a414c5f,4a414c52,534c4c49,534c4c5f,53524c49
  //   ,53524c5f,4245515f,424e455f,4247455f,424c545f,4d554c5f,4c55495f
  //   ,4c425f5f,4c575f5f,4c445f5f,53425f5f,53575f5f,53445f5f,5355425f
  //   ,414e445f,4f525f5f,41444449,41444457
endmodule
