// Digital circuit itype_eq.dig as structural Verilog
module itype_eq (
  input  [6:0] IW_Opcode,
  input  [6:0] Opcode,
  input  [2:0] IW_Funct3,
  input  [2:0] Funct3,
  output EQ
);

  wire add_eq, i_type_eq;

  Comparator #(.Bits(7)) i_type (.a(IW_Opcode), .b(Opcode), .eq(i_type_eq));  // open: gt, lt
  Comparator #(.Bits(3)) add (.a(IW_Funct3), .b(Funct3), .eq(add_eq));  // open: gt, lt
  and and_1 (EQ, i_type_eq, add_eq);
endmodule
