// Digital circuit jalr_eq.dig as structural Verilog
module jalr_eq (
  input  [6:0] IW_Opcode,
  input  [6:0] Opcode,
  input  [2:0] IW_Funct3,
  input  [2:0] Funct3,
  output EQ
);

  wire i_type_eq, Jalr_eq;

  Comparator #(.Bits(7)) i_type (.a(IW_Opcode), .b(Opcode), .eq(i_type_eq));  // open: gt, lt
  Comparator #(.Bits(3)) Jalr (.a(IW_Funct3), .b(Funct3), .eq(Jalr_eq));  // open: gt, lt
  and and_1 (EQ, i_type_eq, Jalr_eq);
endmodule
