// Digital circuit project06.dig as structural Verilog
module project06 (
  input  CLK,
  input  [4:0] PROG,
  input  CLR,
  input  EN,
  output [63:0] A0,
  output [63:0] A1,
  output [63:0] A2,
  output DONE,
  output [63:0] zero,
  output [63:0] ra,
  output [63:0] sp,
  output [63:0] gp,
  output [63:0] tp,
  output [63:0] t0,
  output [63:0] t1,
  output [63:0] t2,
  output [63:0] s0_fp,
  output [63:0] s1,
  output [63:0] a0_2,
  output [63:0] a1_2,
  output [63:0] a2_2,
  output [63:0] a3,
  output [63:0] a4,
  output [63:0] a5,
  output [63:0] a6,
  output [63:0] a7,
  output [63:0] s2,
  output [63:0] s3,
  output [63:0] s4,
  output [63:0] s5,
  output [63:0] s6,
  output [63:0] s7,
  output [63:0] s8,
  output [63:0] s9,
  output [63:0] s10,
  output [63:0] s11,
  output [63:0] t3,
  output [63:0] t4,
  output [63:0] t5,
  output [63:0] t6,
  output [63:0] A3_2
);

  wire ALUSrcA, and_2_out, CLK_t, PCBr, PCSel, Ram, RFW, St, WDSel;
  wire [1:0] Sz;
  wire [2:0] ALUSrcB, BROp;
  wire [3:0] ALUOp;
  wire [4:0] inum, RD, RS1, RS2;
  wire [6:0] alu_1_r_2;
  wire [7:0] inum_1_c0, inum_1_c1, inum_1_c2, inum_1_c3;
  wire [31:0] iw;
  wire [63:0] alu_1_r, imm_I, imm_J, immdecoder_1_imm_b, immdecoder_1_imm_s, immdecoder_1_imm_u,
       multiplexer_1_out, multiplexer_2_out, multiplexer_3_out, multiplexer_4_out, multiplexer_5_out, PC,
       PC_plus_4_s, ramdualport_1_d, read_1_r, register_file_1_rd0, register_file_1_rd1, write_1_r;

  Multiplexer #(.Bits(64)) multiplexer_1 (
    .sel(PCBr), .in_0(PC_plus_4_s), .in_1(multiplexer_5_out), .out(multiplexer_1_out));
  InstDecoder instdecoder_1 (
    .IW(iw), .WDSel(WDSel), .PCSel(PCSel), .ALUSrcB(ALUSrcB), .ALUSrcA(ALUSrcA), .ALUOp(ALUOp), .RFW(RFW),
    .BROp(BROp), .Sz(Sz), .Ram(Ram), .St(St), .INUM(inum));
  inum inum_1 (.c0(inum_1_c0), .c1(inum_1_c1), .c2(inum_1_c2), .c3(inum_1_c3), .inum(inum));
  // Probe on PC
  // Probe on iw
  // Probe on RS1
  // Probe on RS2
  // Probe on RD
  // Probe on imm_I
  // Probe on imm_J
  _64_bit_reg _64_bit_reg_1 (.D(multiplexer_1_out), .CLK(CLK_t), .CLR(CLR), .EN(EN), .Q(PC));
  // Probe on inum_1_c0
  // Probe on inum_1_c1
  // Probe on inum_1_c3
  // Probe on inum_1_c2
  and and_1 (CLK_t, CLK, ~DONE);  // And
  Comparator #(.Bits(32)) END (.a(iw), .b(32'hc0001073), .eq(DONE));  // open: gt, lt
  inst_mem inst_mem_1 (.PROG(PROG), .ADDR(PC[9:2]), .IW(iw));
  Add #(.Bits(64)) PC_plus_4 (.a(PC), .b(64'h4), .c_i(1'b0), .s(PC_plus_4_s));  // open: c_o
  LED led_1 (.in(DONE));
  RegDecoder regdecoder_1 (.IW(iw), .RD(RD), .RS1(RS1), .RS2(RS2));
  and and_2 (and_2_out, RFW, EN);
  Multiplexer #(.Bits(64)) multiplexer_2 (
    .sel(WDSel), .in_0(multiplexer_5_out), .in_1(PC_plus_4_s), .out(multiplexer_2_out));
  Register_File register_file_1 (
    .RR0(RS1), .RR1(RS2), .WriteReg(RD), .WriteEn(and_2_out), .WriteData(multiplexer_2_out), .CLK(CLK_t),
    .CLR(CLR), .RD0(register_file_1_rd0), .RD1(register_file_1_rd1), .x0(zero), .x1(ra), .x2(sp), .x3(gp),
    .x4(tp), .x5(t0), .x6(t1), .x7(t2), .x8(s0_fp), .x9(s1), .x10(A0), .x11(A1), .x12(A2), .x13(a3),
    .x14(a4), .x15(a5), .x16(a6), .x17(a7), .x18(s2), .x19(s3), .x20(s4), .x21(s5), .x22(s6), .x23(s7),
    .x24(s8), .x25(s9), .x26(s10), .x27(s11), .x28(t3), .x29(t4), .x30(t6), .x31(t5));
  ImmDecoder immdecoder_1 (
    .Imm_I(imm_I), .Imm_S(immdecoder_1_imm_s), .Imm_B(immdecoder_1_imm_b), .Imm_U(immdecoder_1_imm_u),
    .Imm_J(imm_J), .IW(iw));
  Multiplexer #(.Bits(64)) multiplexer_3 (
    .sel(ALUSrcA), .in_0(register_file_1_rd0), .in_1(PC), .out(multiplexer_3_out));
  Multiplexer #(.Selector_Bits(3), .Bits(64)) multiplexer_4 (
    .sel(ALUSrcB), .in_0(register_file_1_rd1), .in_1(imm_I), .in_2(imm_J), .in_3(immdecoder_1_imm_s),
    .in_4(immdecoder_1_imm_b), .in_5(immdecoder_1_imm_u), .in_6({64{1'b0}}), .in_7({64{1'b0}}),
    .out(multiplexer_4_out));
  Multiplexer #(.Bits(64)) multiplexer_5 (
    .sel(Ram), .in_0({alu_1_r[63:10], alu_1_r_2, alu_1_r[2:0]}), .in_1(read_1_r), .out(multiplexer_5_out));
  ALU alu_1 (
    .A(multiplexer_3_out), .B(multiplexer_4_out), .ALUOp(ALUOp), .R({alu_1_r[63:10], alu_1_r_2, alu_1_r[2:0]}));
  Branch_Unit branch_unit_1 (.A(register_file_1_rd0), .B(register_file_1_rd1), .BROp(BROp), .PCSel(PCSel), .PCBr(PCBr));
  RAMDualPort #(.AddrBits(7), .Bits(64)) ramdualport_1 (
    .A(alu_1_r_2), .Din(write_1_r), .str(St), .C(CLK_t), .ld(1'b1), .D(ramdualport_1_d));
  Write write_1 (
    .DNew(register_file_1_rd1), .ADDR({alu_1_r[63:10], alu_1_r_2, alu_1_r[2:0]}), .D(ramdualport_1_d),
    .Sz(Sz), .R(write_1_r));
  Read read_1 (.ADDR({alu_1_r[63:10], alu_1_r_2, alu_1_r[2:0]}), .D(ramdualport_1_d), .Sz(Sz), .R(read_1_r));

  assign a0_2 = A0;
  assign a1_2 = A1;
  assign a2_2 = A2;
  assign A3_2 = a3;

  // Other names for the same wires on the sheet: x0[63:0] = zero; x1[63:0] = ra; x2[63:0] = sp; x3[63:0] = gp;
  //   x4[63:0] = tp; x5[63:0] = t0; x6[63:0] = t1; x7[63:0] = t2; x8[63:0] = s0_fp; x9[63:0] = s1; x10[63:0] = A0;
  //   x11[63:0] = A1; x12[63:0] = A2; x13[63:0] = a3; x14[63:0] = a4; x15[63:0] = a5; x16[63:0] = a6; x17[63:0] = a7;
  //   x18[63:0] = s2; x19[63:0] = s3; x20[63:0] = s4; x21[63:0] = s5; x22[63:0] = s6; x23[63:0] = s7; x24[63:0] = s8;
  //   x25[63:0] = s9; x26[63:0] = s10; x27[63:0] = s11; x28[63:0] = t3; x29[63:0] = t4; x30[63:0] = t6;
  //   x31[63:0] = t5

  // Notes on the sheet:
  //   CLK: Hz: 10
endmodule

/* Test case unit-add-i:
CLR EN CLK PROG A0 A1 A2 A3
1   0   0   x    x    x    x    x
0   0   0   x    x    x    x    x
while (!(DONE))
0   1   C   0    x    x    x    x
end while
0   1   0   0 3  0  0  0
*/

/* Test case unit-add-r:
CLR EN CLK PROG A0 A1 A2 A3
1   0   0   x    x    x    x    x
0   0   0   x    x    x    x    x
while (!(DONE))
0   1   C   1    x    x    x    x
end while
0   1   0   1 9  6  0  0
*/

/* Test case unit-jal:
CLR EN CLK PROG A0 A1 A2 A3
1   0   0   x    x    x    x    x
0   0   0   x    x    x    x    x
while (!(DONE))
0   1   C   2    x    x    x    x
end while
0   1   0   2 3  2  0  0
*/

/* Test case unit-mul:
CLR EN CLK PROG A0 A1 A2 A3
1   0   0   x    x    x    x    x
0   0   0   x    x    x    x    x
while (!(DONE))
0   1   C   3    x    x    x    x
end while
0   1   0   3 21  7  0  0
*/

/* Test case unit-sll-r:
CLR EN CLK PROG A0 A1 A2 A3
1   0   0   x    x    x    x    x
0   0   0   x    x    x    x    x
while (!(DONE))
0   1   C   4    x    x    x    x
end while
0   1   0   4 4  1  2  0
*/

/* Test case unit-srl-r:
CLR EN CLK PROG A0 A1 A2 A3
1   0   0   x    x    x    x    x
0   0   0   x    x    x    x    x
while (!(DONE))
0   1   C   5    x    x    x    x
end while
0   1   0   5 4  8  1  0
*/

/* Test case unit-slli:
CLR EN CLK PROG A0 A1 A2 A3
1   0   0   x    x    x    x    x
0   0   0   x    x    x    x    x
while (!(DONE))
0   1   C   6    x    x    x    x
end while
0   1   0   6 8  1  0  0
*/

/* Test case unit-srli:
CLR EN CLK PROG A0 A1 A2 A3
1   0   0   x    x    x    x    x
0   0   0   x    x    x    x    x
while (!(DONE))
0   1   C   7    x    x    x    x
end while
0   1   0   7 8  32  0  0
*/

/* Test case unit-j:
CLR EN CLK PROG A0 A1 A2 A3
1   0   0   x    x    x    x    x
0   0   0   x    x    x    x    x
while (!(DONE))
0   1   C   8    x    x    x    x
end while
0   1   0   8 1  0  0  0
*/

/* Test case unit-beq:
CLR EN CLK PROG A0 A1 A2 A3
1   0   0   x    x    x    x    x
0   0   0   x    x    x    x    x
while (!(DONE))
0   1   C   9    x    x    x    x
end while
0   1   0   9 1  1  0  0
*/

/* Test case unit-blt:
CLR EN CLK PROG A0 A1 A2 A3
1   0   0   x    x    x    x    x
0   0   0   x    x    x    x    x
while (!(DONE))
0   1   C   10    x    x    x    x
end while
0   1   0   10 1  2  0  0
*/

/* Test case unit-bge:
CLR EN CLK PROG A0 A1 A2 A3
1   0   0   x    x    x    x    x
0   0   0   x    x    x    x    x
while (!(DONE))
0   1   C   11    x    x    x    x
end while
0   1   0   11 2  1  0  0
*/

/* Test case unit-sd-ld:
CLR EN CLK PROG A0 A1 A2 A3
1   0   0   x    x    x    x    x
0   0   0   x    x    x    x    x
while (!(DONE))
0   1   C   12    x    x    x    x
end while
0   1   0   12 99  0  0  0
*/

/* Test case unit-sw-lw:
CLR EN CLK PROG A0 A1 A2 A3
1   0   0   x    x    x    x    x
0   0   0   x    x    x    x    x
while (!(DONE))
0   1   C   13    x    x    x    x
end while
0   1   0   13 99  0  0  0
*/

/* Test case unit-sb-lb:
CLR EN CLK PROG A0 A1 A2 A3
1   0   0   x    x    x    x    x
0   0   0   x    x    x    x    x
while (!(DONE))
0   1   C   14    x    x    x    x
end while
0   1   0   14 99  0  0  0
*/

/* Test case prog-quad:
CLR EN CLK PROG A0 A1 A2 A3
1   0   0   x    x    x    x    x
0   0   0   x    x    x    x    x
while (!(DONE))
0   1   C   14    x    x    x    x
end while
0   1   0   14 99  0  0  0
*/

/* Test case get-bitseq:
CLR EN CLK PROG A0 A1 A2 A3
1   0   0   x    x    x    x    x
0   0   0   x    x    x    x    x
while (!(DONE))
0   1   C   16    x    x    x    x
end while
0   1   0   16 6  12  15  0
*/

/* Test case prog-fibrec:
CLR EN CLK PROG A0 A1 A2 A3
1   0   0   x    x    x    x    x
0   0   0   x    x    x    x    x
while (!(DONE))
0   1   C   17    x    x    x    x
end while
0   1   0   17 55  0  0  0
*/

/* Test case prog-is-pal:
CLR EN CLK PROG A0 A1 A2 A3
1   0   0   x    x    x    x    x
0   0   0   x    x    x    x    x
while (!(DONE))
0   1   C   18    x    x    x    x
end while
0   1   0   18 1  3  3  0
*/

/* Test case prog-to-upper:
CLR EN CLK PROG A0 A1 A2 A3
1   0   0   x    x    x    x    x
0   0   0   x    x    x    x    x
while (!(DONE))
0   1   C   19    x    x    x    x
end while
0   1   0   19 5066355251797426176  1014  0  0
*/

/* Test case prog-swap:
CLR EN CLK PROG A0 A1 A2 A3
1   0   0   x    x    x    x    x
0   0   0   x    x    x    x    x
while (!(DONE))
0   1   C   20    x    x    x    x
end while
0   1   0   20 12  1  5  0
*/

/* Test case prog-sort:
CLR EN CLK PROG A0 A1 A2 A3
1   0   0   x    x    x    x    x
0   0   0   x    x    x    x    x
while (!(DONE))
0   1   C   21    x    x    x    x
end while
0   1   0   21 8589934596  25769803784  42949672972  0
*/

/* Test case prog-rstr:
CLR EN CLK PROG A0 A1 A2 A3
1   0   0   x    x    x    x    x
0   0   0   x    x    x    x    x
while (!(DONE))
0   1   C   22    x    x    x    x
end while
0   1   0   22 8241941839440379904  1016  0  0
*/

/* Test case prog-countll:
CLR EN CLK PROG A0 A1 A2 A3
1   0   0   x    x    x    x    x
0   0   0   x    x    x    x    x
while (!(DONE))
0   1   C   23    x    x    x    x
end while
0   1   0   23 3  0  0  0
*/
