// Digital circuit haz.dig as structural Verilog
module haz (
  input  [4:0] RR0_2,
  input  [4:0] WR_3,
  input  RFW_3,
  input  [4:0] WR_4,
  input  RFW_4,
  input  [4:0] RR1_2,
  input  MLD_3,
  input  EN_ORG,
  input  CLR_ORG,
  input  PCbr_2,
  output [1:0] FD_0,
  output [1:0] FD_1,
  output PC_EN,
  output IF_DR_EN,
  output DR_EX_EN,
  output EX_MEM_CLR,
  output IF_EX_CLR,
  output EX_DR_CLR
);

  wire and_1_out, and_2_out, and_3_out, and_4_out, and_5_out, comparator_1_eq, comparator_2_eq,
       comparator_3_eq, comparator_4_eq, comparator_5_eq, comparator_6_eq, not_1_out, not_2_out, or_1_out,
       priorityencoder_1_num;

  Comparator #(.Bits(5)) comparator_1 (.a(RR0_2), .b(WR_3), .eq(comparator_1_eq));  // open: gt, lt
  Comparator #(.Bits(5)) comparator_2 (.a(RR0_2), .b(WR_4), .eq(comparator_2_eq));  // open: gt, lt
  Comparator #(.Bits(5)) comparator_3 (.a(RR1_2), .b(WR_3), .eq(comparator_3_eq));  // open: gt, lt
  Comparator #(.Bits(5)) comparator_4 (.a(RR1_2), .b(WR_4), .eq(comparator_4_eq));  // open: gt, lt
  Comparator #(.Bits(5)) comparator_5 (.a(RR0_2), .b(WR_3), .eq(comparator_5_eq));  // open: gt, lt
  Comparator #(.Bits(5)) comparator_6 (.a(RR1_2), .b(WR_3), .eq(comparator_6_eq));  // open: gt, lt
  and and_1 (and_1_out, comparator_2_eq, RFW_4);
  and and_2 (and_2_out, comparator_4_eq, RFW_4);
  PriorityEncoder priorityencoder_1 (.in0(1'b1), .in1(PCbr_2), .num(priorityencoder_1_num));  // open: any
  and and_3 (and_3_out, comparator_1_eq, RFW_3);
  and and_4 (and_4_out, comparator_3_eq, RFW_3);
  or or_1 (or_1_out, comparator_5_eq, comparator_6_eq);
  not not_1 (not_1_out, priorityencoder_1_num);
  and and_5 (and_5_out, RFW_3, MLD_3, or_1_out);
  Multiplexer multiplexer_1 (.sel(not_1_out), .in_0(1'b1), .in_1(CLR_ORG), .out(IF_EX_CLR));
  PriorityEncoder #(.Selector_Bits(2)) priorityencoder_2 (
    .in0(1'b1), .in1(and_1_out), .in2(and_3_out), .in3(1'b0), .num(FD_0));  // open: any
  PriorityEncoder #(.Selector_Bits(2)) priorityencoder_3 (
    .in0(1'b1), .in1(and_2_out), .in2(and_4_out), .in3(1'b0), .num(FD_1));  // open: any
  Multiplexer multiplexer_2 (.sel(not_1_out), .in_0(1'b1), .in_1(CLR_ORG), .out(EX_DR_CLR));
  not not_2 (not_2_out, and_5_out);
  Multiplexer multiplexer_3 (.sel(not_2_out), .in_0(1'b0), .in_1(EN_ORG), .out(PC_EN));
  Multiplexer multiplexer_4 (.sel(not_2_out), .in_0(1'b0), .in_1(1'b1), .out(DR_EX_EN));
  Multiplexer multiplexer_5 (.sel(not_2_out), .in_0(1'b0), .in_1(1'b1), .out(IF_DR_EN));
  Multiplexer multiplexer_6 (.sel(not_2_out), .in_0(1'b1), .in_1(CLR_ORG), .out(EX_MEM_CLR));
endmodule
