// Digital circuit mem-inst.dig as structural Verilog
module mem_inst (
  input  [7:0] ADDR,
  input  [4:0] PROG,
  output [31:0] IW
);

  wire [31:0] _00, _01, _02, _03, _04, _05, _06, _07, _08;

  ROM #(.AddrBits(8), .Bits(32)) _00_add_3nop (.A(ADDR), .sel(1'b1), .D(_00));
  ROM #(.AddrBits(8), .Bits(32)) _01_add_2nop (.A(ADDR), .sel(1'b1), .D(_01));
  ROM #(.AddrBits(8), .Bits(32)) _02_jal (.A(ADDR), .sel(1'b1), .D(_02));
  ROM #(.AddrBits(8), .Bits(32)) _03_ld (.A(ADDR), .sel(1'b1), .D(_03));
  ROM #(.AddrBits(8), .Bits(32)) _04_add_fwd (.A(ADDR), .sel(1'b1), .D(_04));
  ROM #(.AddrBits(8), .Bits(32)) _05_ld_stl (.A(ADDR), .sel(1'b1), .D(_05));
  ROM #(.AddrBits(8), .Bits(32)) _06_jal_fls (.A(ADDR), .sel(1'b1), .D(_06));
  ROM #(.AddrBits(8), .Bits(32)) _07_branch (.A(ADDR), .sel(1'b1), .D(_07));
  ROM #(.AddrBits(8), .Bits(32)) _08_fibrec (.A(ADDR), .sel(1'b1), .D(_08));
  Multiplexer #(.Selector_Bits(5), .Bits(32)) multiplexer_1 (
    .sel(PROG), .in_0(_00), .in_1(_01), .in_2(_02), .in_3(_03), .in_4(_04), .in_5(_05), .in_6(_06),
    .in_7(_07), .in_8(_08), .in_9({32{1'b0}}), .in_10({32{1'b0}}), .in_11({32{1'b0}}), .in_12({32{1'b0}}),
    .in_13({32{1'b0}}), .in_14({32{1'b0}}), .in_15({32{1'b0}}), .in_16({32{1'b0}}), .in_17({32{1'b0}}),
    .in_18({32{1'b0}}), .in_19({32{1'b0}}), .in_20({32{1'b0}}), .in_21({32{1'b0}}), .in_22({32{1'b0}}),
    .in_23({32{1'b0}}), .in_24({32{1'b0}}), .in_25({32{1'b0}}), .in_26({32{1'b0}}), .in_27({32{1'b0}}),
    .in_28({32{1'b0}}), .in_29({32{1'b0}}), .in_30({32{1'b0}}), .in_31({32{1'b0}}), .out(IW));

  // Notes on the sheet:
  //   contents of _00_add_3nop (hex, n*v repeats v):
  //   300593,13,13,13,400613,13,13,13,c58533,13,13,13,150513,13,13,13
  //   ,c0001073,4*13
  //   contents of _01_add_2nop (hex, n*v repeats v):
  //   300593,13,13,400613,13,13,c58533,13,13,150513,13,13,c0001073,4*13
  //   contents of _02_jal (hex, n*v repeats v):
  //   300593,13,13,400613,13,13,28000ef,4*13,c0001073,4*13,c58533,13,13
  //   ,150513,13,13,8067,4*13
  //   contents of _03_ld (hex, n*v repeats v):
  //   300593,400613,293,13,13,c58533,13,13,a2b023,2b303,13,13,130513
  //   ,c0001073,4*13
  //   contents of _04_add_fwd (hex, n*v repeats v):
  //   300593,400613,c58533,c0001073
  //   contents of _05_ld_stl (hex, n*v repeats v):
  //   513,400593,b53023,53603,160513,c0001073
  //   contents of _06_jal_fls (hex, n*v repeats v):
  //   300513,8000ef,c0001073,450513,8067
  //   contents of _07_branch (hex, n*v repeats v):
  //   300513,700593,b54863,1e00513,4600593,c0001073,150513,c0001073
  //   contents of _08_fibrec (hex, n*v repeats v):
  //   40000113,a00513,8000ef,c0001073,100293,a2c463,8067,fe810113,113023
  //   ,a13423,fff50513,fe5ff0ef,a13823,813503,ffe50513,fd5ff0ef,1013303
  //   ,650533,13083,1810113,8067
endmodule
